// Logisim project main.circ as structural Verilog: 1 circuit, main circuit main
module main (
  input  [7:0] A,
  input  [7:0] B,
  input  [7:0] OPCODE,
  output [7:0] Out,
  output [3:0] Out_flags
);


  // Notes on the sheet:
  //   ALU interface
  //   Last 4 bits - function$OPCODE[4] = carry in$OPCODE[5] = left / right shift$Indexing starts from 0, RTL
  //   - carry out$- overflow$- zero$- negative
endmodule
